// Logisim project project2.circ as structural Verilog: 9 circuits, main circuit CPU
module Adder8Bit (
  input  cin,
  input  [7:0] a,
  input  [7:0] b,
  output [7:0] sum,
  output cout
);

  Adder adder_1 (.a(a), .b(b), .out(sum), .cin(cin), .cout(cout));
endmodule

module General_Purpose_Registers (
  input  [1:0] ReadReg1,
  input  [1:0] WriteReg,
  input  RegWrite,
  input  [7:0] RegDataW,
  input  [1:0] ReadReg2,
  input  Clk,
  output [7:0] RegData1,
  output [7:0] RegData2
);

  wire and_1_out, and_2_out, and_3_out, and_4_out, decoder_1_out0, decoder_1_out1, decoder_1_out2,
       decoder_1_out3;
  wire [7:0] R0_q, R1_q, R2_q, R3_q;

  Decoder #(.select(2)) decoder_1 (
    .out0(decoder_1_out0), .out1(decoder_1_out1), .out2(decoder_1_out2), .out3(decoder_1_out3), .sel(WriteReg));  // open: en
  and and_1 (and_1_out, decoder_1_out0, RegWrite);
  and and_2 (and_2_out, decoder_1_out1, RegWrite);
  and and_3 (and_3_out, decoder_1_out2, RegWrite);
  and and_4 (and_4_out, decoder_1_out3, RegWrite);
  Register R0 (.D(RegDataW), .en(and_1_out), .clk(Clk), .Q(R0_q));  // open: clr
  Register R1 (.D(RegDataW), .en(and_2_out), .clk(Clk), .Q(R1_q));  // open: clr
  Register R2 (.D(RegDataW), .en(and_3_out), .clk(Clk), .Q(R2_q));  // open: clr
  Register R3 (.D(RegDataW), .en(and_4_out), .clk(Clk), .Q(R3_q));  // open: clr
  Multiplexer #(.select(2), .width(8)) multiplexer_1 (
    .in0(R0_q), .in1(R1_q), .in2(R2_q), .in3(R3_q), .out(RegData1), .sel(ReadReg1));
  Multiplexer #(.select(2), .width(8)) multiplexer_2 (
    .in0(R0_q), .in1(R1_q), .in2(R2_q), .in3(R3_q), .out(RegData2), .sel(ReadReg2));
endmodule

module CPU (
);

  wire Clk, Load, LoadImmediate, Op, or_1_out, or_2_out, RegToReg, Store;
  wire [1:0] controlled_buffer_4_out, Ra, Rb, Rt;
  wire [7:0] Addr, alu_1_out_4, controlled_buffer_1_out, controlled_buffer_2_out, Data, Data_Memory_dout,
       general_purpose_registers_1_regdata1, general_purpose_registers_1_regdata2, pc_1_pcaddr;
  wire [15:0] ir_1_instruction_out, rom_1_data;

  Clock clock_1 (.out(Clk));
  RAM #(.asyncread("true")) Data_Memory (
    .addr(Addr), .we(Store), .oe(Load), .clk(Clk), .din(controlled_buffer_2_out), .dout(Data_Memory_dout));
  ROM #(.dataWidth(16)) rom_1 (.addr(pc_1_pcaddr), .data(rom_1_data));
  PC pc_1 (.Clk(Clk), .PCAddr(pc_1_pcaddr));
  assign controlled_buffer_1_out = LoadImmediate ? Data : 8'bz;  // Controlled_Buffer controlled_buffer_1
  assign controlled_buffer_2_out = Store ? general_purpose_registers_1_regdata1 : 8'bz;  // Controlled_Buffer controlled_buffer_2
  assign controlled_buffer_1_out = Load ? Data_Memory_dout : 8'bz;  // Controlled_Buffer controlled_buffer_3
  or or_1 (or_1_out, LoadImmediate, Load, RegToReg);
  assign controlled_buffer_4_out = or_2_out ? Ra : 2'bz;  // Controlled_Buffer controlled_buffer_4
  or or_2 (or_2_out, LoadImmediate, Load);
  assign controlled_buffer_1_out = RegToReg ? alu_1_out_4 : 8'bz;  // Controlled_Buffer controlled_buffer_5
  assign controlled_buffer_4_out = RegToReg ? Rt : 2'bz;  // Controlled_Buffer controlled_buffer_6
  IR ir_1 (.Instruction_In(rom_1_data), .Clk(Clk), .Instruction_Out(ir_1_instruction_out));
  General_Purpose_Registers general_purpose_registers_1 (
    .ReadReg1(Ra), .WriteReg(controlled_buffer_4_out), .RegWrite(or_1_out),
    .RegDataW(controlled_buffer_1_out), .ReadReg2(Rb), .Clk(Clk),
    .RegData1(general_purpose_registers_1_regdata1), .RegData2(general_purpose_registers_1_regdata2));
  Control_Unit control_unit_1 (
    .Instruction(ir_1_instruction_out), .immed8(Data), .addr8(Addr), .Ra(Ra), .Rb(Rb), .Rt(Rt), .op(Op),
    .LoadImmediate(LoadImmediate), .Load(Load), .Store(Store), .RegToReg(RegToReg));
  ALU alu_1 (
    .a(general_purpose_registers_1_regdata1), .b(general_purpose_registers_1_regdata2), .Operation(Op),
    .out_4(alu_1_out_4));

  // Notes on the sheet:
  //   Anna Hauk
  //   CPU:  AnnaBinAnna
  //   I pledge my honor that I have abided by the Stevens Honor System
  //   contents of rom_1 (hex, n*v repeats v):
  //   409 50a 1520 e30 830 602 e31 931 1070 fff
endmodule

module PC (
  input  Clk,
  output [7:0] PCAddr
);

  wire [7:0] adder8bit_1_sum;

  Register register_1 (.D(adder8bit_1_sum), .clk(Clk), .Q(PCAddr));  // open: en, clr
  Adder8Bit adder8bit_1 (.a(PCAddr), .b(8'h1), .sum(adder8bit_1_sum));  // open: cin, cout
endmodule

module IR (
  input  [15:0] Instruction_In,
  input  Clk,
  output [15:0] Instruction_Out
);

  Register #(.width(16)) InstructionRegister (.D(Instruction_In), .clk(Clk), .Q(Instruction_Out));  // open: en, clr
endmodule

module ALU (
  input  [7:0] a,
  input  [7:0] b,
  input  Operation,
  output [7:0] out_4
);

  wire [7:0] adder8bit_1_sum, subtracter8bit_1_difference;

  Adder8Bit adder8bit_1 (.a(a), .b(b), .sum(adder8bit_1_sum));  // open: cin, cout
  Subtracter8Bit subtracter8bit_1 (.a(a), .b(b), .difference(subtracter8bit_1_difference));
  Multiplexer #(.width(8)) multiplexer_1 (
    .in0(adder8bit_1_sum), .in1(subtracter8bit_1_difference), .out(out_4), .sel(Operation));

  // Notes on the sheet:
  //   Operation: 0 = addition, 1 = subtraction
endmodule

module LogicAnd8Bit (
  input  [7:0] b,
  input  [7:0] a,
  output [7:0] out_3
);

  and and_1 (out_3[0], a[0], b[0]);
  and and_2 (out_3[1], a[1], b[1]);
  and and_3 (out_3[2], a[2], b[2]);
  and and_4 (out_3[3], a[3], b[3]);
  and and_5 (out_3[4], a[4], b[4]);
  and and_6 (out_3[5], a[5], b[5]);
  and and_7 (out_3[6], a[6], b[6]);
  and and_8 (out_3[7], a[7], b[7]);
endmodule

module Control_Unit (
  input  [15:0] Instruction,
  output [7:0] immed8,
  output [7:0] addr8,
  output [1:0] Ra,
  output [1:0] Rb,
  output [1:0] Rt,
  output op,
  output LoadImmediate,
  output Load,
  output Store,
  output RegToReg
);

  and and_1 (LoadImmediate, Instruction[10], ~Instruction[11], ~Instruction[12]);  // AND_Gate
  and and_2 (Load, ~Instruction[10], Instruction[11], ~Instruction[12]);  // AND_Gate
  and and_3 (Store, Instruction[10], Instruction[11], ~Instruction[12]);  // AND_Gate
  and and_4 (RegToReg, ~Instruction[11], Instruction[12]);  // AND_Gate

  assign addr8 = Instruction[7:0];
  assign immed8 = Instruction[7:0];
  assign op = Instruction[10];
  assign Ra = Instruction[9:8];
  assign Rb = Instruction[7:6];
  assign Rt = Instruction[5:4];
endmodule

module Subtracter8Bit (
  input  [7:0] a,
  input  [7:0] b,
  output [7:0] difference
);

  Subtractor subtractor_1 (.a(a), .b(b), .out(difference), .bin(1'b0));  // open: bout
endmodule
