// Logisim project 2ram.circ as structural Verilog: 1 circuit, main circuit main
module main (
  output [7:0] out_1
);

  wire clock_1_out;
  wire [7:0] adder_1_out, PC_q;

  Adder adder_1 (.a(8'h1), .b(PC_q), .out(adder_1_out));  // open: cin, cout
  Clock clock_1 (.out(clock_1_out));
  Register PC (.D(adder_1_out), .clk(clock_1_out), .Q(PC_q));  // open: en, clr
  RAM ram_1 (.addr(PC_q), .we(1'b0), .oe(1'b1), .clk(clock_1_out), .dout(out_1));  // open: din

  // Notes on the sheet:
  //   Anna Hauk
  //   I pledge my honor that I have abided by the stevens honor system.
  //   for writing
  //   for reading
endmodule
