// Logisim project regfile.circ as structural Verilog: 1 circuit, main circuit main
// ReadRegData1
module main (
  input  [1:0] ReadReg1,
  input  [1:0] ReadReg2,
  input  [1:0] WriteReg,
  input  RegWrite,
  input  [7:0] RegDataW,
  output [7:0] RegData1,
  output [7:0] RegData2
);

  wire and_1_out, and_2_out, and_3_out, and_4_out, clock_1_out, decoder_1_out0, decoder_1_out1,
       decoder_1_out2, decoder_1_out3;
  wire [7:0] X1_q, X2_q, X3_q, X4_q;

  Clock clock_1 (.out(clock_1_out));
  Decoder #(.select(2)) decoder_1 (
    .out0(decoder_1_out0), .out1(decoder_1_out1), .out2(decoder_1_out2), .out3(decoder_1_out3), .sel(WriteReg));  // open: en
  and and_1 (and_1_out, RegWrite, decoder_1_out0);
  and and_2 (and_2_out, RegWrite, decoder_1_out1);
  and and_3 (and_3_out, RegWrite, decoder_1_out2);
  and and_4 (and_4_out, RegWrite, decoder_1_out3);
  Register X1 (.D(RegDataW), .en(and_1_out), .clk(clock_1_out), .Q(X1_q));  // open: clr
  Register X2 (.D(RegDataW), .en(and_2_out), .clk(clock_1_out), .Q(X2_q));  // open: clr
  Register X3 (.D(RegDataW), .en(and_3_out), .clk(clock_1_out), .Q(X3_q));  // open: clr
  Register X4 (.D(RegDataW), .en(and_4_out), .clk(clock_1_out), .Q(X4_q));  // open: clr
  Multiplexer #(.select(2), .width(8)) multiplexer_1 (
    .in0(X1_q), .in1(X2_q), .in2(X3_q), .in3(X4_q), .out(RegData1), .sel(ReadReg1));
  Multiplexer #(.select(2), .width(8)) multiplexer_2 (
    .in0(X1_q), .in1(X2_q), .in2(X3_q), .in3(X4_q), .out(RegData2), .sel(ReadReg2));

  // Notes on the sheet:
  //   Anna Hauk
  //   I pledge my honor that I have abided by the Stevens Honor System.
endmodule
